# Fritzing sketch pcb - top + bottom (saved by Fritzing 0.9.2b)
breadboards: 1

parts:
  JP_top_+5V0_DC = Header 1 [package=1x01_offset]
  JP_top_V_rect = Header 1 [package=1x01_offset]
  JP_top_V_test = Header 1 [package=1x01_offset]
  JP_top_neg_02 = Header 1 [package=1x01_offset]
  JP_top_neg_01 = Header 1 [package=1x01_offset]
  top_5V0_DC_out = Header 2 [package=molex-1x2_lock]
  330μ1 = Capacitor Polarized [package=panasonic_g]  # not connected
  22μ1 = Capacitor Polarized [package=panasonic_d]  # not connected
  1N4148 = Diode [package=diode-1n4001]  # not connected
  IRF7319_1 = MOSFET-NCHANNEL-SOIC8 [package=so08]  # not connected
  IRF7319_2 = MOSFET-NCHANNEL-SOIC8 [package=so08]  # not connected
  BZG03C24 = Zener Diode [part_number=1N4732A breakdown_voltage=3.6V package="Melf DO-213 AB [SMD]"]  # not connected
  BZG03C24_2 = Zener Diode [part_number=1N4732A breakdown_voltage=3.6V package="Melf DO-213 AB [SMD]"]  # not connected
  JPbottom_neg_02 = Header 1 [package=1x01_offset]
  bottom_AC_in = Header 2 [package=molex-1x2_lock]
  JP_top_+5V0_DC_2 = Header 1 [package=1x01_offset]
  JP_bottom_V_rect = Header 1 [package=1x01_offset]
  JP_bottom_V_test = Header 1 [package=1x01_offset]
  JP_bottom_neg_01 = Header 1 [package=1x01_offset]
  Recom_R-78B5_0-1_1 = Voltage Regulator [package=to-220-alt]  # not connected
  1N4149 = Diode [package=diode-1n4001]  # not connected

nets:
  5V0 DC: JP_top_+5V0_DC.1, top_5V0_DC_out.1, JP_top_+5V0_DC_2.1
  V rect: JP_top_V_rect.1, JP_bottom_V_rect.1
  V test: JP_top_V_test.1, JP_bottom_V_test.1
  top GND: JP_top_neg_02.1, JP_top_neg_01.1, top_5V0_DC_out.2
  bottom GND: JPbottom_neg_02.1, JP_bottom_neg_01.1
  AC in 0: bottom_AC_in.2

notes:
  +
  ~
  -
  down
  IRF7319
  bottom
  čos
  up
  top
  hrvoje ivanic
  2016
  bottom pcb
  top pcb
